// Logisim project ex5.circ as structural Verilog: 5 circuits, main circuit rotr
module rotr (
  input  [15:0] A,
  input  [3:0] B,
  output [15:0] Out1
);

  wire not_1_out, not_2_out, not_3_out, not_4_out;
  wire [15:0] rot1_1_out_3, rot2_1_out_3, rot4_1_out_3;

  not not_1 (not_1_out, B[0]);
  rot1 rot1_1 (.in_1(A), .in_2(not_1_out), .out_3(rot1_1_out_3));
  not not_2 (not_2_out, B[1]);
  rot2 rot2_1 (.in_1(rot1_1_out_3), .in_2(not_2_out), .out_3(rot2_1_out_3));
  not not_3 (not_3_out, B[2]);
  not not_4 (not_4_out, B[3]);
  rot4 rot4_1 (.in_1(rot2_1_out_3), .in_2(not_3_out), .out_3(rot4_1_out_3));
  rot8 rot8_1 (.in_1(rot4_1_out_3), .in_2(not_4_out), .out_3(Out1));

  // Notes on the sheet:
  //   PUT CIRCUITRY HERE
endmodule

module rot8 (
  input  [15:0] in_1,
  input  in_2,
  output [15:0] out_3
);

  wire [15:0] rot4_1_out_3;

  rot4 rot4_1 (.in_1(in_1), .in_2(in_2), .out_3(rot4_1_out_3));
  rot4 rot4_2 (.in_1(rot4_1_out_3), .in_2(in_2), .out_3(out_3));

  // Notes on the sheet:
  //   PUT CIRCUITRY HERE
endmodule

module rot4 (
  input  [15:0] in_1,
  input  in_2,
  output [15:0] out_3
);

  wire [15:0] rot2_1_out_3;

  rot2 rot2_1 (.in_1(in_1), .in_2(in_2), .out_3(rot2_1_out_3));
  rot2 rot2_2 (.in_1(rot2_1_out_3), .in_2(in_2), .out_3(out_3));

  // Notes on the sheet:
  //   PUT CIRCUITRY HERE
endmodule

module rot2 (
  input  [15:0] in_1,
  input  in_2,
  output [15:0] out_3
);

  wire [15:0] rot1_1_out_3;

  rot1 rot1_1 (.in_1(in_1), .in_2(in_2), .out_3(rot1_1_out_3));
  rot1 rot1_2 (.in_1(rot1_1_out_3), .in_2(in_2), .out_3(out_3));

  // Notes on the sheet:
  //   PUT CIRCUITRY HERE
endmodule

module rot1 (
  input  [15:0] in_1,
  input  in_2,
  output [15:0] out_3
);

  Multiplexer #(.width(16), .enable("false")) multiplexer_1 (
    .in0({in_1[0], in_1[15:1]}), .in1(in_1), .out(out_3), .sel(in_2));

  // Notes on the sheet:
  //   PUT CIRCUITRY HERE
endmodule
