// Logisim project alu.circ as structural Verilog: 1 circuit, main circuit alu
// As
module alu (
  input  [31:0] A,
  input  [31:0] B,
  input  [3:0] ALUSel,
  output [31:0] Result
);

  wire comparator_1_lt, comparator_2_eq, xor_2_out;
  wire [4:0] bit_extender_1_out, bit_extender_2_out, bit_extender_3_out;
  wire [31:0] add0, andBlock, divUnsigned, mulh, mulhu, mull, multiplexer_2_out, multiplexer_3_out,
       multiplexer_4_out, multiplier_3_cout, multiplier_3_out, negator_1_out, negator_2_out, negator_3_out,
       orBlock, remu, slLogical, slThan, srArith, srLogical, sub, subtractor_2_out, xorBlock;

  assign andBlock = A & B;  // AND_Gate and_1, 32 bits wide
  assign orBlock = A | B;  // OR_Gate or_1, 32 bits wide
  Bit_Extender #(.in_width(32), .out_width(5)) bit_extender_1 (.in(B), .out(bit_extender_1_out));
  Bit_Extender #(.in_width(32), .out_width(5)) bit_extender_2 (.in(B), .out(bit_extender_2_out));
  Bit_Extender #(.in_width(32), .out_width(5)) bit_extender_3 (.in(B), .out(bit_extender_3_out));
  Adder #(.width(32)) adder_1 (.a(A), .b(B), .out(add0));  // open: cin, cout
  assign xorBlock = A ^ B;  // XOR_Gate xor_1, 32 bits wide
  Shifter #(.width(32), .shift("lr")) shifter_1 (.in(A), .\dist (bit_extender_1_out), .out(srLogical));
  Shifter #(.width(32), .shift("ar")) shifter_2 (.in(A), .\dist (bit_extender_2_out), .out(srArith));
  Shifter #(.width(32)) shifter_3 (.in(A), .\dist (bit_extender_3_out), .out(slLogical));
  Multiplexer #(.select(4), .width(32), .enable("false")) multiplexer_1 (
    .in0(add0), .in1(andBlock), .in2(orBlock), .in3(xorBlock), .in4(srLogical), .in5(srArith),
    .in6(slLogical), .in7(slThan), .in8(divUnsigned), .in9(remu), .in10(mull), .in11(mulhu), .in12(sub),
    .in13(B), .in14(mulh), .in15({32{1'b0}}), .out(Result));  // open: sel
  Comparator #(.width(32)) comparator_1 (.a(A), .b(B), .lt(comparator_1_lt));  // open: gt, eq
  Divider #(.width(32)) divider_1 (.a(A), .b(B), .out(divUnsigned));  // open: upper, rem
  Divider #(.width(32)) divider_2 (.a(A), .b(B), .rem(remu));  // open: out, upper
  Multiplier #(.width(32)) multiplier_1 (.a(A), .b(B), .out(mull));  // open: cin, cout
  Multiplier #(.width(32)) multiplier_2 (.a(A), .b(B), .cout(mulhu));  // open: out, cin
  Subtractor #(.width(32)) subtractor_1 (.a(A), .b(B), .out(sub));  // open: bin, bout
  assign slThan = {{31{1'b0}}, comparator_1_lt};  // Bit_Extender bit_extender_4
  Negator #(.width(32)) negator_1 (.in(A), .out(negator_1_out));
  Negator #(.width(32)) negator_2 (.in(B), .out(negator_2_out));
  Multiplexer #(.width(32), .enable("false")) multiplexer_2 (
    .in0(A), .in1(negator_1_out), .out(multiplexer_2_out), .sel(A[31]));
  Multiplexer #(.width(32), .enable("false")) multiplexer_3 (
    .in0(B), .in1(negator_2_out), .out(multiplexer_3_out), .sel(B[31]));
  Multiplier #(.width(32)) multiplier_3 (
    .a(multiplexer_2_out), .b(multiplexer_3_out), .out(multiplier_3_out), .cout(multiplier_3_cout));  // open: cin
  xor xor_2 (xor_2_out, A[31], B[31]);
  Comparator #(.width(32)) comparator_2 (.a({32{1'b0}}), .b(multiplier_3_out), .eq(comparator_2_eq));  // open: gt, lt
  Negator #(.width(32)) negator_3 (.in(multiplier_3_cout), .out(negator_3_out));
  Subtractor #(.width(32)) subtractor_2 (.a(negator_3_out), .b(32'h1), .out(subtractor_2_out));  // open: bin, bout
  Multiplexer #(.width(32), .enable("false")) multiplexer_4 (
    .in0(subtractor_2_out), .in1(negator_3_out), .out(multiplexer_4_out), .sel(comparator_2_eq));
  Multiplexer #(.width(32), .enable("false")) multiplexer_5 (
    .in0(multiplier_3_cout), .in1(multiplexer_4_out), .out(mulh), .sel(xor_2_out));

  // Other names for the same wires on the sheet: As = A[31]; Bs = B[31]

  // Notes on the sheet:
  //   INPUTS to your circuit
  //   DON'T CHANGE THE LOCATIONS OF THE INPUTS AND OUTPUTS!
  //   OUTPUT from your circuit
endmodule
