// Logisim project control_logic.circ as structural Verilog: 1 circuit, main circuit control_logic
module control_logic (
  input  [31:0] inst,
  input  BrEq,
  input  BrLt,
  output PCSel,
  output RegWEn,
  output [2:0] ImmSel,
  output BrUn,
  output ASel,
  output BSel,
  output [3:0] ALUSel,
  output MemRW,
  output [1:0] WBSel
);

  wire add, and_20_out, and_21_out, and_22_out, and_23_out, and_24_out, and_r, auipc, beq, bge, bgeu, blt,
       bltu, bne, bsel_t, comparator_1_eq, comparator_2_eq, comparator_3_eq, comparator_4_eq,
       comparator_5_eq, comparator_6_eq, comparator_7_eq, comparator_8_eq, comparator_9_eq, comparator_10_eq,
       comparator_11_eq, comparator_12_eq, comparator_13_eq, comparator_14_eq, comparator_16_eq,
       comparator_17_eq, comparator_18_eq, comparator_19_eq, comparator_20_eq, comparator_21_eq,
       comparator_22_eq, comparator_23_eq, comparator_24_eq, comparator_25_eq, comparator_27_eq,
       comparator_28_eq, comparator_29_eq, comparator_30_eq, comparator_31_eq, comparator_32_eq,
       comparator_33_eq, comparator_35_eq, comparator_36_eq, comparator_40_eq, comparator_42_eq,
       comparator_43_eq, comparator_44_eq, comparator_45_eq, comparator_46_eq, comparator_47_eq, divu, I,
       jalr, lw3, mul, mulh, mulhu, not_2_out, not_3_out, not_4_out, nothing, or_7_out, or_r, R, remu, SB,
       sll_r, slt, sra_r, srl_r, sub, U, xor_r;
  wire [2:0] multiplexer_2_out, multiplexer_4_out, multiplexer_6_out;
  wire [3:0] multiplexer_1_out, multiplexer_3_out, multiplexer_5_out, multiplexer_7_out, multiplexer_8_out,
       multiplexer_10_out, multiplexer_11_out, multiplexer_12_out, multiplexer_13_out, multiplexer_14_out,
       multiplexer_15_out, multiplexer_16_out, multiplexer_17_out, multiplexer_18_out;

  Comparator #(.width(3)) comparator_1 (.a(inst[14:12]), .b(3'b101), .eq(comparator_1_eq));  // open: gt, lt
  Comparator #(.width(7)) comparator_2 (.a(inst[31:25]), .b({7{1'b0}}), .eq(comparator_2_eq));  // open: gt, lt
  Comparator #(.width(3)) comparator_3 (.a(inst[14:12]), .b(3'b000), .eq(comparator_3_eq));  // open: gt, lt
  Comparator #(.width(7)) comparator_4 (.a(inst[31:25]), .b(7'b0000001), .eq(comparator_4_eq));  // open: gt, lt
  Comparator #(.width(3)) comparator_5 (.a(inst[14:12]), .b(3'b000), .eq(comparator_5_eq));  // open: gt, lt
  Comparator #(.width(7)) comparator_6 (.a(inst[31:25]), .b(7'b0100000), .eq(comparator_6_eq));  // open: gt, lt
  Comparator #(.width(3)) comparator_7 (.a(inst[14:12]), .b(3'b000), .eq(comparator_7_eq));  // open: gt, lt
  Comparator #(.width(7)) comparator_8 (.a(inst[31:25]), .b({7{1'b0}}), .eq(comparator_8_eq));  // open: gt, lt
  Comparator #(.width(3)) comparator_9 (.a(inst[14:12]), .b(3'b100), .eq(comparator_9_eq));  // open: gt, lt
  Comparator #(.width(7)) comparator_10 (.a(inst[31:25]), .b(7'b0000001), .eq(comparator_10_eq));  // open: gt, lt
  Comparator #(.width(3)) comparator_11 (.a(inst[14:12]), .b(3'b101), .eq(comparator_11_eq));  // open: gt, lt
  Comparator #(.width(7)) comparator_12 (.a(inst[31:25]), .b({7{1'b0}}), .eq(comparator_12_eq));  // open: gt, lt
  Comparator #(.width(7)) comparator_13 (.a(inst[31:25]), .b({7{1'b0}}), .eq(comparator_13_eq));  // open: gt, lt
  Comparator #(.width(3)) comparator_14 (.a(inst[14:12]), .b(3'b111), .eq(comparator_14_eq));  // open: gt, lt
  Comparator #(.width(7)) comparator_15 (.a(7'b0110111), .b(inst[6:0]), .eq(bsel_t));  // open: gt, lt
  and and_1 (add, comparator_2_eq, comparator_3_eq, R);
  and and_2 (mul, comparator_4_eq, comparator_5_eq, R);
  and and_3 (srl_r, comparator_12_eq, comparator_1_eq, R);
  and and_4 (and_r, comparator_13_eq, comparator_14_eq, R);
  and and_5 (sub, comparator_6_eq, comparator_7_eq, R);
  and and_6 (xor_r, comparator_8_eq, comparator_9_eq, R);
  and and_7 (divu, comparator_10_eq, comparator_11_eq, R);
  or or_1 (RegWEn, R, I, U, WBSel[1]);
  Comparator #(.width(3)) comparator_16 (.a(inst[14:12]), .b(3'b001), .eq(comparator_16_eq));  // open: gt, lt
  Comparator #(.width(3)) comparator_17 (.a(inst[14:12]), .b(3'b001), .eq(comparator_17_eq));  // open: gt, lt
  Comparator #(.width(3)) comparator_18 (.a(inst[14:12]), .b(3'b011), .eq(comparator_18_eq));  // open: gt, lt
  Comparator #(.width(3)) comparator_19 (.a(inst[14:12]), .b(3'b010), .eq(comparator_19_eq));  // open: gt, lt
  Comparator #(.width(3)) comparator_20 (.a(inst[14:12]), .b(3'b101), .eq(comparator_20_eq));  // open: gt, lt
  Comparator #(.width(3)) comparator_21 (.a(inst[14:12]), .b(3'b110), .eq(comparator_21_eq));  // open: gt, lt
  Comparator #(.width(7)) comparator_22 (.a(inst[31:25]), .b(7'b0001111), .eq(comparator_22_eq));  // open: gt, lt
  Comparator #(.width(3)) comparator_23 (.a(inst[14:12]), .b(3'b000), .eq(comparator_23_eq));  // open: gt, lt
  Comparator #(.width(7)) comparator_24 (.a(inst[31:25]), .b(7'b0000001), .eq(comparator_24_eq));  // open: gt, lt
  Comparator #(.width(3)) comparator_25 (.a(inst[14:12]), .b(3'b111), .eq(comparator_25_eq));  // open: gt, lt
  Multiplexer #(.width(4), .enable("false")) multiplexer_1 (
    .in0(4'b0000), .in1(4'b0001), .out(multiplexer_1_out), .sel(and_r));
  Multiplexer #(.width(3), .enable("false")) multiplexer_2 (
    .in0(3'b000), .in1(3'b001), .out(multiplexer_2_out), .sel(MemRW));
  Comparator #(.width(7)) comparator_26 (.a(inst[6:0]), .b(7'b0110011), .eq(R));  // open: gt, lt
  Comparator #(.width(7)) comparator_27 (.a(inst[31:25]), .b({7{1'b0}}), .eq(comparator_27_eq));  // open: gt, lt
  Comparator #(.width(7)) comparator_28 (.a(inst[31:25]), .b(7'b0000001), .eq(comparator_28_eq));  // open: gt, lt
  Comparator #(.width(7)) comparator_29 (.a(inst[31:25]), .b(7'b0000001), .eq(comparator_29_eq));  // open: gt, lt
  Comparator #(.width(7)) comparator_30 (.a(inst[31:25]), .b({7{1'b0}}), .eq(comparator_30_eq));  // open: gt, lt
  Comparator #(.width(7)) comparator_31 (.a(inst[31:25]), .b(7'b0100000), .eq(comparator_31_eq));  // open: gt, lt
  Comparator #(.width(7)) comparator_32 (.a(inst[31:25]), .b({7{1'b0}}), .eq(comparator_32_eq));  // open: gt, lt
  Multiplexer #(.width(4), .enable("false")) multiplexer_3 (
    .in0(multiplexer_1_out), .in1(4'b0010), .out(multiplexer_3_out), .sel(or_r));
  Multiplexer #(.width(3), .enable("false")) multiplexer_4 (
    .in0(multiplexer_2_out), .in1(3'b010), .out(multiplexer_4_out), .sel(SB));
  and and_8 (sll_r, comparator_27_eq, comparator_16_eq, R);
  and and_9 (mulh, comparator_28_eq, comparator_17_eq, R);
  and and_10 (mulhu, comparator_29_eq, comparator_18_eq, R);
  and and_11 (slt, comparator_30_eq, comparator_19_eq, R);
  and and_12 (sra_r, comparator_31_eq, comparator_20_eq, R);
  and and_13 (or_r, comparator_32_eq, comparator_21_eq, R);
  and and_14 (nothing, comparator_22_eq, comparator_23_eq, R);
  and and_15 (remu, comparator_24_eq, comparator_25_eq, R);
  not not_1 (BSel, R);
  Multiplexer #(.width(4), .enable("false")) multiplexer_5 (
    .in0(multiplexer_3_out), .in1(4'b0011), .out(multiplexer_5_out), .sel(xor_r));
  Multiplexer #(.width(3), .enable("false")) multiplexer_6 (
    .in0(multiplexer_4_out), .in1(3'b011), .out(multiplexer_6_out), .sel(U));
  Multiplexer #(.width(4), .enable("false")) multiplexer_7 (
    .in0(multiplexer_5_out), .in1(4'b0100), .out(multiplexer_7_out), .sel(srl_r));
  Multiplexer #(.width(4), .enable("false")) multiplexer_8 (
    .in0(multiplexer_7_out), .in1(4'b0101), .out(multiplexer_8_out), .sel(sra_r));
  Multiplexer #(.width(3), .enable("false")) multiplexer_9 (
    .in0(multiplexer_6_out), .in1(3'b100), .out(ImmSel), .sel(WBSel[1]));
  Comparator #(.width(7)) comparator_33 (.a(inst[6:0]), .b(7'b0010011), .eq(comparator_33_eq));  // open: gt, lt
  or or_2 (ASel, SB, auipc, WBSel[1]);
  Multiplexer #(.width(4), .enable("false")) multiplexer_10 (
    .in0(multiplexer_8_out), .in1(4'b0110), .out(multiplexer_10_out), .sel(sll_r));
  Comparator #(.width(7)) comparator_34 (.a(inst[6:0]), .b(7'b0000011), .eq(lw3));  // open: gt, lt
  Comparator #(.width(7)) comparator_35 (.a(inst[6:0]), .b(7'b1100111), .eq(comparator_35_eq));  // open: gt, lt
  Comparator #(.width(3)) comparator_36 (.a(inst[14:12]), .b(3'b000), .eq(comparator_36_eq));  // open: gt, lt
  Multiplexer #(.width(4), .enable("false")) multiplexer_11 (
    .in0(multiplexer_10_out), .in1(4'b0111), .out(multiplexer_11_out), .sel(slt));
  and and_16 (jalr, comparator_35_eq, comparator_36_eq);
  Multiplexer #(.width(4), .enable("false")) multiplexer_12 (
    .in0(multiplexer_11_out), .in1(4'b1000), .out(multiplexer_12_out), .sel(divu));
  or or_3 (I, lw3, comparator_33_eq, jalr);
  or or_4 (WBSel[0], jalr, lw3);
  or or_5 (BrUn, bltu, bgeu);
  Multiplexer #(.width(4), .enable("false")) multiplexer_13 (
    .in0(multiplexer_12_out), .in1(4'b1001), .out(multiplexer_13_out), .sel(remu));
  Multiplexer #(.width(4), .enable("false")) multiplexer_14 (
    .in0(multiplexer_13_out), .in1(4'b1010), .out(multiplexer_14_out), .sel(mul));
  Multiplexer #(.width(4), .enable("false")) multiplexer_15 (
    .in0(multiplexer_14_out), .in1(4'b1011), .out(multiplexer_15_out), .sel(mulhu));
  Multiplexer #(.width(4), .enable("false")) multiplexer_16 (
    .in0(multiplexer_15_out), .in1(4'b1100), .out(multiplexer_16_out), .sel(sub));
  Multiplexer #(.width(4), .enable("false")) multiplexer_17 (
    .in0(multiplexer_16_out), .in1(4'b1101), .out(multiplexer_17_out), .sel(bsel_t));
  Comparator #(.width(7)) comparator_37 (.a(inst[6:0]), .b(7'b0100011), .eq(MemRW));  // open: gt, lt
  Comparator #(.width(7)) comparator_38 (.a(inst[6:0]), .b(7'b1100011), .eq(SB));  // open: gt, lt
  Comparator #(.width(7)) comparator_39 (.a(inst[6:0]), .b(7'b0010111), .eq(auipc));  // open: gt, lt
  Comparator #(.width(7)) comparator_40 (.a(inst[6:0]), .b(7'b0110111), .eq(comparator_40_eq));  // open: gt, lt
  Comparator #(.width(7)) comparator_41 (.a(inst[6:0]), .b(7'b1101111), .eq(WBSel[1]));  // open: gt, lt
  Comparator #(.width(3)) comparator_42 (.a(inst[14:12]), .b(3'b100), .eq(comparator_42_eq));  // open: gt, lt
  Multiplexer #(.width(4), .enable("false")) multiplexer_18 (
    .in0(multiplexer_17_out), .in1(4'b1110), .out(multiplexer_18_out), .sel(mulh));
  or or_6 (U, auipc, comparator_40_eq);
  Comparator #(.width(3)) comparator_43 (.a(inst[14:12]), .b(3'b000), .eq(comparator_43_eq));  // open: gt, lt
  and and_17 (beq, comparator_43_eq, SB);
  Comparator #(.width(3)) comparator_44 (.a(inst[14:12]), .b(3'b001), .eq(comparator_44_eq));  // open: gt, lt
  and and_18 (bne, comparator_44_eq, SB);
  and and_19 (blt, comparator_42_eq, SB);
  Multiplexer #(.width(4), .enable("false")) multiplexer_19 (
    .in0(multiplexer_18_out), .in1(4'b1111), .out(ALUSel), .sel(nothing));
  not not_2 (not_2_out, BrEq);
  not not_3 (not_3_out, BrLt);
  not not_4 (not_4_out, BrEq);
  or or_7 (or_7_out, bgeu, bge);
  and and_20 (and_20_out, beq, BrEq);
  and and_21 (and_21_out, not_2_out, bne);
  and and_22 (and_22_out, not_3_out, not_4_out, or_7_out);
  and and_23 (and_23_out, blt, BrLt);
  and and_24 (and_24_out, BrLt, bltu);
  or or_8 (PCSel, and_22_out, jalr, WBSel[1], and_20_out, and_21_out, and_23_out, and_24_out);
  Comparator #(.width(3)) comparator_45 (.a(inst[14:12]), .b(3'b101), .eq(comparator_45_eq));  // open: gt, lt
  Comparator #(.width(3)) comparator_46 (.a(inst[14:12]), .b(3'b110), .eq(comparator_46_eq));  // open: gt, lt
  Comparator #(.width(3)) comparator_47 (.a(inst[14:12]), .b(3'b111), .eq(comparator_47_eq));  // open: gt, lt
  and and_25 (bge, comparator_45_eq, SB);
  and and_26 (bltu, comparator_46_eq, SB);
  and and_27 (bgeu, comparator_47_eq, SB);

  // Other names for the same wires on the sheet: opcode[6:0] = inst[6:0]; imm7_31[24:0] = inst[31:7];
  //   rd[4:0] = inst[11:7]; func3[2:0] = inst[14:12]; rs1[4:0] = inst[19:15]; rs2[4:0] = inst[24:20];
  //   func7[6:0] = inst[31:25]; S = MemRW; UJ = WBSel[1]

  // Notes on the sheet:
  //   INPUTS to your circuit
  //   DON'T CHANGE THE LOCATIONS OF THE INPUTS AND OUTPUTS!
  //   OUTPUT from your circuit
  //   SB type instruction
endmodule
