// Logisim project imm_gen.circ as structural Verilog: 1 circuit, main circuit imm_gen
module imm_gen (
  input  [31:0] inst,
  input  [2:0] ImmSel,
  output [31:0] imm
);

  wire [31:0] I_type, R_type;

  assign I_type = {{20{inst[31]}}, inst[31:20]};  // Bit_Extender bit_extender_1
  assign R_type = {{25{inst[24]}}, inst[24:18]};  // Bit_Extender bit_extender_2
  Multiplexer #(.select(3), .width(32), .enable("false")) multiplexer_1 (
    .in0(I_type), .in5(R_type), .out(imm), .sel(ImmSel));  // open: in1, in2, in3, in4, in6, in7

  // Notes on the sheet:
  //   INPUTS to your circuit
  //   DON'T CHANGE THE LOCATIONS OF THE INPUTS AND OUTPUTS!
  //   OUTPUT from your circuit
endmodule
